// Logisim project ti74138.circ as structural Verilog: 1 circuit, main circuit main
module main (
  input  in_1,
  input  in_2,
  input  in_3,
  input  in_4,
  input  in_5,
  input  in_6,
  input  in_7,
  input  in_8,
  input  in_9,
  input  in_10,
  input  in_11,
  input  in_12,
  output out_13,
  output out_14,
  output out_15,
  output out_16,
  output out_17,
  output out_18,
  output out_19,
  output out_20
);

  wire and_1_out, and_2_out, decoder_1_out0, decoder_1_out1, decoder_1_out2, decoder_1_out3, decoder_1_out4,
       decoder_1_out5, decoder_1_out6, decoder_1_out7;
  wire [7:0] decoder_2_out0, multiplexer_1_out, not_1_out;

  and and_1 (and_1_out, ~in_1, ~in_2, in_3);  // AND_Gate
  Decoder #(.select(3), .disabled(0), .enable("false")) decoder_1 (
    .out0(decoder_1_out0), .out1(decoder_1_out1), .out2(decoder_1_out2), .out3(decoder_1_out3),
    .out4(decoder_1_out4), .out5(decoder_1_out5), .out6(decoder_1_out6), .out7(decoder_1_out7),
    .sel({in_6, in_5, in_4}));
  nand nand_1 (out_13, and_1_out, decoder_1_out0);
  nand nand_2 (out_14, and_1_out, decoder_1_out1);
  nand nand_3 (out_15, and_1_out, decoder_1_out2);
  nand nand_4 (out_16, and_1_out, decoder_1_out3);
  nand nand_5 (out_17, and_1_out, decoder_1_out4);
  nand nand_6 (out_18, and_1_out, decoder_1_out5);
  nand nand_7 (out_19, and_1_out, decoder_1_out6);
  nand nand_8 (out_20, and_1_out, decoder_1_out7);
  Decoder #(.select(3), .disabled(0), .enable("false")) decoder_2 (
    .out0(decoder_2_out0[0]), .out1(decoder_2_out0[1]), .out2(decoder_2_out0[2]), .out3(decoder_2_out0[3]),
    .out4(decoder_2_out0[4]), .out5(decoder_2_out0[5]), .out6(decoder_2_out0[6]), .out7(decoder_2_out0[7]),
    .sel({in_9, in_8, in_7}));
  and and_2 (and_2_out, ~in_10, ~in_11, in_12);  // AND_Gate
  Multiplexer #(.width(8), .disabled(0), .enable("false")) multiplexer_1 (
    .in0({8{1'b1}}), .in1(not_1_out), .out(multiplexer_1_out), .sel(and_2_out));
  assign not_1_out = ~decoder_2_out0;  // NOT_Gate not_1, 8 bits wide
endmodule
