// Logisim project ti74181.circ as structural Verilog: 1 circuit, main circuit main
module main (
  input  c0,
  input  m,
  input  a0_n,
  input  b0_n,
  input  a1_n,
  input  b1_n,
  input  a2_n,
  input  b2_n,
  input  a3_n,
  input  b3_n,
  input  s0,
  input  s1,
  input  s2,
  input  s3,
  output f0_n,
  output f1_n,
  output a_b,
  output f2_n,
  output f3_n,
  output p_n,
  output c4,
  output g_n
);

  wire and_1_out, and_2_out, and_3_out, and_4_out, and_5_out, and_6_out, and_7_out, and_8_out, and_9_out,
       and_10_out, and_11_out, and_13_out, and_14_out, and_15_out, and_16_out, and_17_out, and_18_out,
       and_19_out, and_20_out, and_21_out, and_22_out, and_23_out, and_24_out, and_25_out, and_26_out,
       and_27_out, and_28_out, and_29_out, and_30_out, and_31_out, and_32_out, and_33_out, nand_1_out,
       nand_3_out, nor_1_out, nor_2_out, nor_3_out, nor_4_out, nor_5_out, nor_6_out, nor_7_out, nor_8_out,
       nor_9_out, nor_10_out, nor_11_out, not_1_out;

  nand nand_1 (nand_1_out, c0, not_1_out);
  not not_1 (not_1_out, m);
  and and_1 (and_1_out, not_1_out, nor_1_out);
  and and_2 (and_2_out, ~nor_1_out, nor_3_out);  // AND_Gate
  xor xor_1 (f0_n, nand_1_out, and_2_out);
  and and_3 (and_3_out, s1, ~b0_n);  // AND_Gate
  and and_4 (and_4_out, b0_n, s0);
  nor nor_1 (nor_1_out, a0_n, and_4_out, and_3_out);
  and and_5 (and_5_out, not_1_out, nor_3_out, c0);
  and and_6 (and_6_out, ~nor_4_out, nor_6_out);  // AND_Gate
  nor nor_2 (nor_2_out, and_1_out, and_5_out);
  xor xor_2 (f1_n, nor_2_out, and_6_out);
  and and_7 (and_7_out, a0_n, b0_n, s3);
  and and_8 (and_8_out, ~b0_n, s2, a0_n);  // AND_Gate
  nor nor_3 (nor_3_out, and_8_out, and_7_out);
  and and_9 (and_9_out, b1_n, s0);
  nor nor_4 (nor_4_out, a1_n, and_9_out, and_13_out);
  and and_10 (and_10_out, not_1_out, nor_4_out);
  and and_11 (and_11_out, not_1_out, nor_1_out, nor_6_out);
  and and_12 (a_b, f0_n, f1_n, f2_n, f3_n);
  and and_13 (and_13_out, s1, ~b1_n);  // AND_Gate
  and and_14 (and_14_out, not_1_out, c0, nor_3_out, nor_6_out);
  nor nor_5 (nor_5_out, and_10_out, and_11_out, and_14_out);
  xor xor_3 (f2_n, nor_5_out, and_17_out);
  and and_15 (and_15_out, a1_n, s3, b1_n);
  and and_16 (and_16_out, ~b1_n, s2, a1_n);  // AND_Gate
  nor nor_6 (nor_6_out, and_16_out, and_15_out);
  and and_17 (and_17_out, ~nor_7_out, nor_9_out);  // AND_Gate
  and and_18 (and_18_out, b2_n, s0);
  nor nor_7 (nor_7_out, a2_n, and_18_out, and_22_out);
  and and_19 (and_19_out, not_1_out, nor_7_out);
  and and_20 (and_20_out, not_1_out, nor_4_out, nor_9_out);
  and and_21 (and_21_out, ~b2_n, s2, a2_n);  // AND_Gate
  and and_22 (and_22_out, s1, ~b2_n);  // AND_Gate
  and and_23 (and_23_out, not_1_out, nor_1_out, nor_6_out, nor_9_out);
  nor nor_8 (nor_8_out, and_19_out, and_20_out, and_23_out, and_25_out);
  and and_24 (and_24_out, a2_n, s3, b2_n);
  nor nor_9 (nor_9_out, and_21_out, and_24_out);
  and and_25 (and_25_out, not_1_out, c0, nor_3_out, nor_6_out, nor_9_out);
  and and_26 (and_26_out, ~nor_10_out, nor_11_out);  // AND_Gate
  xor xor_4 (f3_n, nor_8_out, and_26_out);
  and and_27 (and_27_out, s1, ~b3_n);  // AND_Gate
  and and_28 (and_28_out, b3_n, s0);
  nor nor_10 (nor_10_out, a3_n, and_28_out, and_27_out);
  nand nand_2 (p_n, nor_3_out, nor_6_out, nor_9_out, nor_11_out);
  nand nand_3 (nand_3_out, c0, nor_3_out, nor_6_out, nor_9_out, nor_11_out);
  or or_1 (c4, ~nand_3_out, ~g_n);  // OR_Gate
  and and_29 (and_29_out, ~b3_n, s2, a3_n);  // AND_Gate
  and and_30 (and_30_out, a3_n, s3, b3_n);
  nor nor_11 (nor_11_out, and_29_out, and_30_out);
  and and_31 (and_31_out, nor_1_out, nor_6_out, nor_9_out, nor_11_out);
  and and_32 (and_32_out, nor_4_out, nor_9_out, nor_11_out);
  and and_33 (and_33_out, nor_7_out, nor_11_out);
  nor nor_12 (g_n, and_31_out, and_32_out, and_33_out, nor_10_out);
endmodule
