// Logisim project ti74377.circ as structural Verilog: 1 circuit, main circuit main
module main (
  input  en,
  input  d0,
  input  d1,
  input  d2,
  input  in_5,
  input  in_6,
  input  in_7,
  input  in_8,
  input  in_9,
  output q0,
  output q0_n,
  output q1,
  output q1_n,
  output q2,
  output q2_n,
  output q3,
  output out_17,
  output out_18,
  output out_19,
  output out_20,
  output out_21,
  output out_22,
  output out_23,
  output out_24,
  output out_25
);

  wire and_1_out, and_2_out, and_3_out, and_4_out, and_5_out, and_6_out, and_7_out, and_8_out, and_9_out,
       and_10_out, and_11_out, and_12_out, and_13_out, and_14_out, and_15_out, and_16_out, clock_1_out,
       or_1_out, or_2_out, or_3_out, or_4_out, or_5_out, or_6_out, or_7_out, or_8_out;

  and and_1 (and_1_out, en, d0);
  and and_2 (and_2_out, ~en, q0);  // AND_Gate
  and and_3 (and_3_out, en, d1);
  and and_4 (and_4_out, ~en, q1);  // AND_Gate
  and and_5 (and_5_out, en, d2);
  and and_6 (and_6_out, ~en, q2);  // AND_Gate
  and and_7 (and_7_out, en, in_5);
  and and_8 (and_8_out, ~en, q3);  // AND_Gate
  and and_9 (and_9_out, en, in_6);
  and and_10 (and_10_out, ~en, out_18);  // AND_Gate
  and and_11 (and_11_out, en, in_7);
  and and_12 (and_12_out, ~en, out_20);  // AND_Gate
  and and_13 (and_13_out, en, in_8);
  and and_14 (and_14_out, ~en, out_22);  // AND_Gate
  and and_15 (and_15_out, en, in_9);
  and and_16 (and_16_out, ~en, out_24);  // AND_Gate
  Clock clock_1 (.out(clock_1_out));
  or or_1 (or_1_out, and_1_out, and_2_out);
  or or_2 (or_2_out, and_3_out, and_4_out);
  or or_3 (or_3_out, and_5_out, and_6_out);
  or or_4 (or_4_out, and_7_out, and_8_out);
  or or_5 (or_5_out, and_9_out, and_10_out);
  or or_6 (or_6_out, and_11_out, and_12_out);
  or or_7 (or_7_out, and_13_out, and_14_out);
  or or_8 (or_8_out, and_15_out, and_16_out);
  D_Flip_Flop d_ff_1 (.clk(clock_1_out), .D(or_1_out), .Q(q0), .Qn(q0_n), .en(1'b1));  // open: preset, reset
  D_Flip_Flop d_ff_2 (.clk(clock_1_out), .D(or_2_out), .Q(q1), .Qn(q1_n), .en(1'b1));  // open: preset, reset
  D_Flip_Flop d_ff_3 (.clk(clock_1_out), .D(or_3_out), .Q(q2), .Qn(q2_n), .en(1'b1));  // open: preset, reset
  D_Flip_Flop d_ff_4 (.clk(clock_1_out), .D(or_4_out), .Q(q3), .Qn(out_17), .en(1'b1));  // open: preset, reset
  D_Flip_Flop d_ff_5 (.clk(clock_1_out), .D(or_5_out), .Q(out_18), .Qn(out_19), .en(1'b1));  // open: preset, reset
  D_Flip_Flop d_ff_6 (.clk(clock_1_out), .D(or_6_out), .Q(out_20), .Qn(out_21), .en(1'b1));  // open: preset, reset
  D_Flip_Flop d_ff_7 (.clk(clock_1_out), .D(or_7_out), .Q(out_22), .Qn(out_23), .en(1'b1));  // open: preset, reset
  D_Flip_Flop d_ff_8 (.clk(clock_1_out), .D(or_8_out), .Q(out_24), .Qn(out_25), .en(1'b1));  // open: preset, reset
endmodule
